# Fritzing sketch splate (saved by Fritzing 0.9.3b)

parts:
  Часть1 = Arduino Uno (Rev3)
  Часть2 = KY-033 Tracing Black White Line Hunting Sensor Module For Arduino  # not connected
  S1 = H-Bridge with L298N
  Часть3 = KY-033 Tracing Black White Line Hunting Sensor Module For Arduino  # not connected
  M1 = DC Motor
  M2 = DC Motor
  BAT1 = 18650 battery holder [package=battery-18650-kit]
  BAT2 = 18650 battery holder [package=battery-18650-kit]  # not connected
  Raspberry_Pi1 = Raspberry Pi B+  # not connected
  M3 = RioRand LM2596  # not connected
  BAT3 = 18650 battery holder [package=battery-18650-kit]  # not connected
  BAT4 = 18650 battery holder [package=battery-18650-kit]  # not connected
  BAT5 = 18650 battery holder [package=battery-18650-kit]  # not connected
  BAT6 = 18650 battery holder [package=battery-18650-kit]  # not connected
  BAT7 = 18650 battery holder [package=battery-18650-kit]  # not connected

nets:
  N1: Часть1.D3_PWM, S1.ENB
  N2: Часть1.D4, S1.IN4
  N3: Часть1.D5_PWM, S1.IN3
  N4: Часть1.D6_PWM, S1.IN2
  N5: Часть1.D7, S1.IN1
  N6: S1.12V, BAT1.+
  N7: S1.M1-01, M1.pin_2
  N8: S1.M1-02, M1.pin_1
  N9: S1.M2-01, M2.pin_2
  N10: S1.M2-02, M2.pin_1

custom parts:
  KY-033 Tracing Black White Line Hunting Sensor Module For Arduino: Tracing Black White Line Hunting Sensor Module For Arduino Description: This is KY-033 tracking sensor. The KY-033 measures the intensity of infrared radiation and delivers it as an analog output voltage. Features: Operating voltage: 2.5 - 12V(cannot over12V) working current: 18mA-20mA at 5V Enhanced accuracy Documents: http://www.vishay.com/docs/83760/tcrt5000.pdf
  H-Bridge with L298N: h-bridge
  18650 battery holder: 18650 Battery Holder
