# Fritzing sketch splate_v2 (saved by Fritzing 0.9.3b)

parts:
  Часть1 = Arduino Uno (Rev3)
  Часть2 = KY-033 Tracing Black White Line Hunting Sensor Module For Arduino
  S1 = H-Bridge with L298N
  Часть3 = KY-033 Tracing Black White Line Hunting Sensor Module For Arduino
  M1 = DC Motor
  M2 = DC Motor
  BAT1 = 18650 battery holder [package=battery-18650-kit]
  BAT2 = 18650 battery holder [package=battery-18650-kit]  # not connected
  Raspberry_Pi1 = Raspberry Pi B+  # not connected
  M3 = RioRand LM2596  # not connected
  BAT3 = 18650 battery holder [package=battery-18650-kit]  # not connected
  BAT4 = 18650 battery holder [package=battery-18650-kit]  # not connected
  BAT5 = 18650 battery holder [package=battery-18650-kit]  # not connected
  BAT6 = 18650 battery holder [package=battery-18650-kit]  # not connected
  BAT7 = 18650 battery holder [package=battery-18650-kit]  # not connected
  U1 = SWITCH_SPDT [package=kps-1290]

nets:
  N1: Часть1.A0, Часть2.S
  N2: Часть1.A1, Часть3.S
  GND: Часть1.GND, Часть2.GND
  N3: Часть1.D3_PWM, S1.ENB
  N4: Часть1.D4, S1.IN4
  N5: Часть1.D5_PWM, S1.IN3
  N6: Часть1.D6_PWM, S1.IN2
  N7: Часть1.D7, S1.IN1
  N8: Часть1.5V, Часть2.V+
  N9: S1.12V, U1.S
  N10: S1.M1-01, M1.pin_2
  N11: S1.M1-02, M1.pin_1
  N12: S1.M2-01, M2.pin_2
  N13: S1.M2-02, M2.pin_1
  N14: BAT1.+, U1.O

custom parts:
  KY-033 Tracing Black White Line Hunting Sensor Module For Arduino: Tracing Black White Line Hunting Sensor Module For Arduino Description: This is KY-033 tracking sensor. The KY-033 measures the intensity of infrared radiation and delivers it as an analog output voltage. Features: Operating voltage: 2.5 - 12V(cannot over12V) working current: 18mA-20mA at 5V Enhanced accuracy Documents: http://www.vishay.com/docs/83760/tcrt5000.pdf
  H-Bridge with L298N: h-bridge
  18650 battery holder: 18650 Battery Holder
